# Fritzing sketch input_output (saved by Fritzing 0.9.4)
breadboards: 1

parts:
  Bauteil1 = Tessel 2
  U1 = Optocoupler [package=THT]
  R1 = Resistor [tolerance=±5% resistance=330 package=THT]
  R2 = Resistor [tolerance=±5% resistance=330 package=THT]
  R4 = Resistor [tolerance=±5% resistance=10k package=THT]
  R5 = Resistor [tolerance=±5% resistance=10k package=THT]
  U2 = Optocoupler [package=THT]
  IC1 = IC, DIP package, 16 pins [chip_label=CS2105GP-M12]

nets:
  N1: Bauteil1.GND#28, R4.Pin_1
  N2: Bauteil1.3V3#29, U1.Pin_5
  N3: Bauteil1.2#32, U1.Pin_4, R4.Pin_0
  N4: Bauteil1.GND#38, R5.Pin_1
  N5: Bauteil1.3V3#39, U2.Pin_5
  N6: Bauteil1.2#42, R5.Pin_0, U2.Pin_4
  N7: U1.Pin_2, R1.Pin_1, R2.Pin_1, U2.Pin_2, IC1.pin14
  N8: R1.Pin_0, IC1.pin7
  N9: R2.Pin_0, IC1.pin11

custom parts:
  Tessel 2: Draft version of Tessel 2
